# Fritzing sketch Assignment1IOTok (saved by Fritzing 0.9.3b)
breadboards: 1

parts:
  U1 = NodeMCU V1.0
  Mod1 = KY-018 Photoresistor Module [package="Breakout board"]
  Mod2 = KY-011 Two Color LED Module [package="Breakout board"]
  R2 = Resistor [tolerance=±5% resistance=200 package=THT]
  R3 = Resistor [tolerance=±5% resistance=200 package=THT]
  Mod3 = KY-012 Active Buzzer Module [package="Breakout board"]
  Mod4 = KY-004 Key Switch Module [package="Breakout board"]
  R5 = Resistor [tolerance=±5% resistance=100 package=THT]

nets:
  N1: U1.D1, R2.Pin_1
  N2: U1.D2, R3.Pin_1
  N3: U1.D3, Mod4.S
  N4: U1.D4, Mod3.-
  N5: U1.3V3, Mod1.-, R5.Pin_0
  GND: U1.GND, Mod1.Vin, Mod2.-, Mod4.-
  N6: U1.A0, Mod1.S
  N7: Mod2.Vin, R3.Pin_0
  N8: Mod2.S, R2.Pin_0
  N9: Mod3.S, R5.Pin_1

custom parts:
  NodeMCU V1.0: ESP8266 based NodeMCU
  KY-018 Photoresistor Module: KY-018 Photoresistor module, used to measure light intensity. It can determine the presence or absence of light.
  KY-011 Two Color LED Module: KY-011 Two Color LED Module consist of a common cathode 3mm red/green LED.
  KY-012 Active Buzzer Module: Active Piezoelectric Buzzer Module KY-012, it produces single-tone sound when signal is high. (Special thanks to vanepp for fixing the PCB holes and other errors)
  KY-004 Key Switch Module: Arduino Key Switch Module Keyes KY-004 is a push button that will output a high signal when pressed.
